// Logisim project CPU_monocycle.circ as structural Verilog: 11 circuits, main circuit main
module main (
  input  Reset,
  output [31:0] Instr,
  output RegWrite,
  output [4:0] RegAddr,
  output [31:0] RegData,
  output MemWrite,
  output [4:0] MemAddr,
  output [31:0] MemData
);

  wire ALUSrc, clock_1_out, clock_2_out, clock_3_out, not_1_out, Z;
  wire [1:0] DataSrc, ExtOp, NPC_Sel, RegDst;
  wire [2:0] ALUOp;
  wire [31:0] C, Dout, Ext_ext, multiplexer_3_out, PC, Register_File_rd1;

  // Probe on RegAddr
  // Probe on RegData
  IFU IFU (
    .NPC_Sel(NPC_Sel), .Z(Z), .Jr({C[31:7], MemAddr, C[1:0]}), .Clk(clock_1_out), .Reset(Reset),
    .Instr(Instr), .PC(PC));
  Clock clock_1 (.out(clock_1_out));
  Multiplexer #(.select(2), .width(5), .enable("false")) multiplexer_1 (
    .in0(Instr[15:11]), .in1(Instr[20:16]), .in2({5{1'b1}}), .out(RegAddr), .sel(RegDst));  // open: in3
  Multiplexer #(.select(2), .width(32), .enable("false")) multiplexer_2 (
    .in0({C[31:7], MemAddr, C[1:0]}), .in1(Dout), .in2(PC), .out(RegData), .sel(DataSrc));  // open: in3
  GRF Register_File (
    .A1(Instr[25:21]), .A2(Instr[20:16]), .A3(RegAddr), .Wd(RegData), .We(RegWrite), .Clk(clock_2_out),
    .Reset(Reset), .Rd1(Register_File_rd1), .Rd2(MemData));
  Clock clock_2 (.out(clock_2_out));
  Controller Controller (
    .OpCode(Instr[31:26]), .Funct(Instr[5:0]), .RegDst(RegDst), .ALUSrc(ALUSrc), .DataSrc(DataSrc),
    .RegWrite(RegWrite), .MemWrite(MemWrite), .NPC_Sel(NPC_Sel), .ExtOp(ExtOp), .ALUOp(ALUOp));
  EXT Ext (.Imm(Instr[15:0]), .ExtOp(ExtOp), .Ext(Ext_ext));
  Multiplexer #(.width(32), .enable("false")) multiplexer_3 (
    .in0(MemData), .in1(Ext_ext), .out(multiplexer_3_out), .sel(ALUSrc));
  ALU ALU (
    .A(Register_File_rd1), .B(multiplexer_3_out), .ALUOp(ALUOp), .C({C[31:7], MemAddr, C[1:0]}), .Z(Z));  // open: N, V, Carry
  Clock clock_3 (.out(clock_3_out));
  not not_1 (not_1_out, MemWrite);
  RAM #(.addrWidth(5), .dataWidth(32), .bus("separate")) ram_1 (
    .addr(MemAddr), .din(MemData), .data(Dout), .str(MemWrite), .clk(clock_3_out), .ld(not_1_out), .clr(Reset));  // open: sel

  // Other names for the same wires on the sheet: A1[4:0] = Instr[25:21]; A2[4:0] = Instr[20:16];
  //   A3[4:0] = Instr[15:11]; I[15:0] = Instr[15:0]; C[6:2] = MemAddr; Funct[5:0] = Instr[5:0];
  //   OpCode[5:0] = Instr[31:26]
endmodule

module Controller (
  input  [5:0] OpCode,
  input  [5:0] Funct,
  output [1:0] RegDst,
  output ALUSrc,
  output [1:0] DataSrc,
  output RegWrite,
  output MemWrite,
  output [1:0] NPC_Sel,
  output [1:0] ExtOp,
  output [2:0] ALUOp
);

  wire addiu, addu, addu_out, and_5_out, and_6_out, and_7_out, and_8_out, and_9_out, and_10_out, and_11_out,
       beq, j, jal, jr, jr_out, lui, lw, not_1_out, not_2_out, not_3_out, not_4_out, not_5_out, not_6_out,
       not_7_out, not_8_out, not_9_out, not_10_out, not_11_out, not_12_out, ori, pull_resistor_1_node, R_out,
       slt, slt_out, subu, subu_out, sw;

  not not_1 (not_1_out, OpCode[5]);
  not not_2 (not_2_out, Funct[5]);
  not not_3 (not_3_out, OpCode[4]);
  not not_4 (not_4_out, OpCode[3]);
  not not_5 (not_5_out, OpCode[2]);
  not not_6 (not_6_out, OpCode[1]);
  not not_7 (not_7_out, OpCode[0]);
  not not_8 (not_8_out, Funct[4]);
  not not_9 (not_9_out, Funct[3]);
  not not_10 (not_10_out, Funct[2]);
  not not_11 (not_11_out, Funct[1]);
  not not_12 (not_12_out, Funct[0]);
  and R (R_out, not_1_out, not_3_out, not_4_out, not_5_out, not_6_out, not_7_out);
  and u_jr (jr_out, not_2_out, not_8_out, Funct[3], not_10_out, not_11_out, not_12_out);
  and and_1 (jr, R_out, jr_out);
  and u_addu (addu_out, Funct[5], not_8_out, not_9_out, not_10_out, not_11_out, Funct[0]);
  and and_2 (addu, R_out, addu_out);
  and u_subu (subu_out, Funct[5], not_8_out, not_9_out, not_10_out, Funct[1], Funct[0]);
  and and_3 (subu, R_out, subu_out);
  and u_slt (slt_out, Funct[5], not_8_out, Funct[3], not_10_out, Funct[1], not_12_out);
  and and_4 (slt, R_out, slt_out);
  // AND_Gate and_5 has open pins: out=and_5_out
  and and_6 (and_6_out, R_out, and_5_out);
  // AND_Gate and_7 has open pins: out=and_7_out
  and and_8 (and_8_out, R_out, and_7_out);
  and u_beq (beq, not_1_out, not_3_out, not_4_out, OpCode[2], not_6_out, not_7_out);
  and u_addiu (addiu, not_1_out, not_3_out, OpCode[3], not_5_out, not_6_out, OpCode[0]);
  and u_ori (ori, not_1_out, not_3_out, OpCode[3], OpCode[2], not_6_out, OpCode[0]);
  and u_lui (lui, not_1_out, not_3_out, OpCode[3], OpCode[2], OpCode[1], OpCode[0]);
  and u_lw (lw, OpCode[5], not_3_out, not_4_out, not_5_out, OpCode[1], OpCode[0]);
  and u_sw (sw, OpCode[5], not_3_out, OpCode[3], not_5_out, OpCode[1], OpCode[0]);
  // AND_Gate and_9 has open pins: out=and_9_out
  // AND_Gate and_10 has open pins: out=and_10_out
  and u_j (j, not_1_out, not_3_out, not_4_out, not_5_out, OpCode[1], not_7_out);
  and u_jal (jal, not_1_out, not_3_out, not_4_out, not_5_out, OpCode[1], OpCode[0]);
  Pull_Resistor pull_resistor_1 (.node(pull_resistor_1_node));
  // AND_Gate and_11 has open pins: out=and_11_out
  or or_1 (RegDst[0], beq, addiu, ori, lui, lw, sw);
  buf or_2 (RegDst[1], jal);  // OR_Gate
  or or_3 (ALUSrc, addiu, ori, lui, lw, sw);
  or or_4 (DataSrc[0], lw, sw);
  buf or_5 (DataSrc[1], jal);  // OR_Gate
  or or_6 (RegWrite, addu, subu, slt, addiu, ori, lui, lw, jal);
  buf or_7 (MemWrite, sw);  // OR_Gate
  or or_8 (NPC_Sel[0], jr, j, jal);
  or or_9 (NPC_Sel[1], jr, beq);
  buf or_10 (ExtOp[0], pull_resistor_1_node);  // OR_Gate
  buf or_11 (ExtOp[1], lui);  // OR_Gate
  or or_12 (ALUOp[0], addu, addiu, lui, lw, sw);
  or or_13 (ALUOp[1], subu, slt, beq, lui);
  or or_14 (ALUOp[2], jr, slt, ori, lui);
endmodule

module GRF (
  input  We,
  input  [4:0] A1,
  input  [4:0] A2,
  input  [4:0] A3,
  input  [31:0] Wd,
  input  Clk,
  input  Reset,
  output [31:0] Rd1,
  output [31:0] Rd2
);

  wire decoder_1_out0, decoder_1_out1, decoder_1_out2, decoder_1_out3, decoder_1_out4, decoder_1_out5,
       decoder_1_out6, decoder_1_out7;
  wire [31:0] RAM_4_0_a, RAM_4_0_b, ram_4_1_a, ram_4_1_b, ram_4_2_a, ram_4_2_b, ram_4_3_a, ram_4_3_b,
       ram_4_4_a, ram_4_4_b, ram_4_5_a, ram_4_5_b, ram_4_6_a, ram_4_6_b, ram_4_7_a, ram_4_7_b;

  Multiplexer #(.select(3), .width(32)) multiplexer_1 (
    .in0(RAM_4_0_b), .in1(ram_4_1_b), .in2(ram_4_2_b), .in3(ram_4_3_b), .in4(ram_4_4_b), .in5(ram_4_5_b),
    .in6(ram_4_6_b), .in7(ram_4_7_b), .out(Rd2), .sel(A2[4:2]));  // open: en
  Multiplexer #(.select(3), .width(32)) multiplexer_2 (
    .in0(RAM_4_0_a), .in1(ram_4_1_a), .in2(ram_4_2_a), .in3(ram_4_3_a), .in4(ram_4_4_a), .in5(ram_4_5_a),
    .in6(ram_4_6_a), .in7(ram_4_7_a), .out(Rd1), .sel(A1[4:2]));  // open: en
  RAM_4_0 RAM_4_0 (
    .reset(Reset), .C(Wd), .A(RAM_4_0_a), .B(RAM_4_0_b), .clk(Clk), .select_A(A1[1:0]), .select_B(A2[1:0]),
    .select_C(A3[1:0]), .WE(decoder_1_out0));
  RAM_4 ram_4_1 (
    .reset(Reset), .C(Wd), .A(ram_4_1_a), .B(ram_4_1_b), .clk(Clk), .select_A(A1[1:0]), .select_B(A2[1:0]),
    .select_C(A3[1:0]), .WE(decoder_1_out1));
  RAM_4 ram_4_2 (
    .reset(Reset), .C(Wd), .A(ram_4_2_a), .B(ram_4_2_b), .clk(Clk), .select_A(A1[1:0]), .select_B(A2[1:0]),
    .select_C(A3[1:0]), .WE(decoder_1_out2));
  RAM_4 ram_4_3 (
    .reset(Reset), .C(Wd), .A(ram_4_3_a), .B(ram_4_3_b), .clk(Clk), .select_A(A1[1:0]), .select_B(A2[1:0]),
    .select_C(A3[1:0]), .WE(decoder_1_out3));
  RAM_4 ram_4_4 (
    .reset(Reset), .C(Wd), .A(ram_4_4_a), .B(ram_4_4_b), .clk(Clk), .select_A(A1[1:0]), .select_B(A2[1:0]),
    .select_C(A3[1:0]), .WE(decoder_1_out4));
  RAM_4 ram_4_5 (
    .reset(Reset), .C(Wd), .A(ram_4_5_a), .B(ram_4_5_b), .clk(Clk), .select_A(A1[1:0]), .select_B(A2[1:0]),
    .select_C(A3[1:0]), .WE(decoder_1_out5));
  RAM_4 ram_4_6 (
    .reset(Reset), .C(Wd), .A(ram_4_6_a), .B(ram_4_6_b), .clk(Clk), .select_A(A1[1:0]), .select_B(A2[1:0]),
    .select_C(A3[1:0]), .WE(decoder_1_out6));
  RAM_4 ram_4_7 (
    .reset(Reset), .C(Wd), .A(ram_4_7_a), .B(ram_4_7_b), .clk(Clk), .select_A(A1[1:0]), .select_B(A2[1:0]),
    .select_C(A3[1:0]), .WE(decoder_1_out7));
  Decoder #(.select(3), .disabled(0)) decoder_1 (
    .out0(decoder_1_out0), .out1(decoder_1_out1), .out2(decoder_1_out2), .out3(decoder_1_out3),
    .out4(decoder_1_out4), .out5(decoder_1_out5), .out6(decoder_1_out6), .out7(decoder_1_out7),
    .sel(A3[4:2]), .en(We));

  // Other names for the same wires on the sheet: select_A[2:0] = A1[4:2]; select_B[2:0] = A2[4:2]
endmodule

module IFU (
  input  [1:0] NPC_Sel,
  input  Z,
  input  Clk,
  input  Reset,
  input  [31:0] Jr,
  output [31:0] Instr,
  output [31:0] PC
);

  wire [29:0] adder_1_out, adder_2_out, multiplexer_1_out, multiplexer_2_out, PC_t;

  Adder_part #(.width(30)) adder_1 (.a(PC_t), .b(30'h1), .out(adder_1_out));  // open: cin, cout
  Adder_part #(.width(30)) adder_2 (.a(adder_1_out), .b(multiplexer_1_out), .out(adder_2_out));  // open: cin, cout
  Multiplexer #(.width(30)) multiplexer_1 (
    .in0({30{1'b0}}), .in1({{15{Instr[15]}}, Instr[14:0]}), .out(multiplexer_1_out), .sel(Z));  // open: en
  Multiplexer #(.select(2), .width(30)) multiplexer_2 (
    .in0(adder_1_out), .in1({PC_t[29:26], Instr[25:0]}), .in2(adder_2_out), .in3(Jr[31:2]),
    .out(multiplexer_2_out), .sel(NPC_Sel));  // open: en
  // Probe on multiplexer_2_out
  Register #(.width(30)) u_PC (.D(multiplexer_2_out), .Q(PC_t), .clk(Clk), .clr(Reset));  // open: en
  Adder_part #(.width(30)) adder_3 (.a(PC_t), .b(30'h1), .out(PC[31:2]));  // open: cin, cout
  ROM #(.addrWidth(5), .dataWidth(32)) rom_1 (.addr(PC_t[4:0]), .data(Instr));  // open: sel

  assign PC[1:0] = 2'b00;

  // Notes on the sheet:
  //   contents of rom_1 (hex, n*v repeats v):
  //   24102000 2408000a ae100000 ae080004 26090008 ad290000 1084821 ac09200c 11080001 24080001 25080001
  //   ac082010 11300001 24080001 25080001 ac082014 3c010000 34210001 1014023 ac082018 24090006 352a0001
  //   ac0a2024 3c080002 ac08202c 800001b 24080008 ac082038 8c082004 ac08203c
endmodule

module ALU (
  input  [2:0] ALUOp,
  input  [31:0] A,
  input  [31:0] B,
  output [31:0] C,
  output N,
  output Z,
  output V,
  output Carry
);

  wire or_2_out;
  wire [0:0] comparator_1_lt;
  wire [1:0] adder_1_v, subtracter_1_v;
  wire [31:0] adder_1_c, and_1_out, or_1_out, subtracter_1_c, xor_1_out;

  Adder adder_1 (.A(A), .B(B), .C(adder_1_c), .V(adder_1_v));
  Subtracter subtracter_1 (.A(A), .C(subtracter_1_c), .B(B), .V(subtracter_1_v));
  assign and_1_out = A & B;  // AND_Gate and_1, 32 bits wide
  assign or_1_out = A | B;  // OR_Gate or_1, 32 bits wide
  assign xor_1_out = A ^ B;  // XOR_Gate xor_1, 32 bits wide
  Comparator #(.width(32)) comparator_1 (.a(A), .b(B), .lt(comparator_1_lt[0]));  // open: gt, eq
  Multiplexer #(.select(3), .width(2)) multiplexer_1 (
    .in0(2'b00), .in1(adder_1_v), .in2(subtracter_1_v), .in3(2'b00), .in4(2'b00), .in5(2'b00), .in6(2'b00),
    .in7(2'b00), .out({Carry, V}), .sel(ALUOp));  // open: en
  or or_2 (or_2_out, C[0], C[1], C[2], C[3], C[4], C[5], C[6], C[7], C[8], C[9], C[10], C[11], C[12], C[13], C[14], C[15], C[17], C[18], C[19], C[20], C[21], C[22], C[23], C[24], C[25], C[26], C[27], C[28], C[29], C[30], C[31], C[16]);
  not not_1 (Z, or_2_out);
  Multiplexer #(.select(3), .width(32)) multiplexer_2 (
    .in0({32{1'b0}}), .in1(adder_1_c), .in2(subtracter_1_c), .in3(and_1_out), .in4(or_1_out),
    .in5(xor_1_out), .in6({{31{1'b0}}, comparator_1_lt[0]}), .in7(B), .out(C), .sel(ALUOp));  // open: en

  assign N = C[31];
endmodule

module DM (
  input  [31:0] Addr,
  input  [31:0] Din,
  input  Clk,
  input  We,
  input  Reset,
  output [31:0] Dout
);

  wire not_1_out;

  RAM #(.addrWidth(5), .dataWidth(32), .bus("separate")) ram_1 (
    .addr(Addr[6:2]), .din(Din), .data(Dout), .str(We), .clk(Clk), .ld(not_1_out), .clr(Reset));  // open: sel
  not not_1 (not_1_out, We);
endmodule

module EXT (
  input  [15:0] Imm,
  input  [1:0] ExtOp,
  output [31:0] Ext
);

  Multiplexer #(.select(2), .width(32)) multiplexer_1 (
    .in0({{16{1'b0}}, Imm}), .in1({{17{Imm[15]}}, Imm[14:0]}), .in2({Imm, {16{1'b0}}}), .in3({32{1'b0}}),
    .out(Ext), .sel(ExtOp));  // open: en
endmodule

module RAM_4 (
  input  clk,
  input  [1:0] select_A,
  input  [1:0] select_B,
  input  reset,
  input  [1:0] select_C,
  input  WE,
  input  [31:0] C,
  output [31:0] A,
  output [31:0] B
);

  wire decoder_1_out0, decoder_1_out1, decoder_1_out2, decoder_1_out3;
  wire [31:0] register_1_q, register_2_q, register_3_q, register_4_q;

  Decoder #(.select(2), .disabled(0)) decoder_1 (
    .out0(decoder_1_out0), .out1(decoder_1_out1), .out2(decoder_1_out2), .out3(decoder_1_out3),
    .sel(select_C), .en(WE));
  Register #(.width(32)) register_1 (.D(C), .en(decoder_1_out0), .Q(register_1_q), .clk(clk), .clr(reset));
  Register #(.width(32)) register_2 (.D(C), .en(decoder_1_out1), .Q(register_2_q), .clk(clk), .clr(reset));
  Register #(.width(32)) register_3 (.D(C), .en(decoder_1_out2), .Q(register_3_q), .clk(clk), .clr(reset));
  Register #(.width(32)) register_4 (.D(C), .en(decoder_1_out3), .Q(register_4_q), .clk(clk), .clr(reset));
  Multiplexer #(.select(2), .width(32)) multiplexer_1 (
    .in0(register_1_q), .in1(register_2_q), .in2(register_3_q), .in3(register_4_q), .out(A), .sel(select_A));  // open: en
  Multiplexer #(.select(2), .width(32)) multiplexer_2 (
    .in0(register_1_q), .in1(register_2_q), .in2(register_3_q), .in3(register_4_q), .out(B), .sel(select_B));  // open: en
endmodule

module RAM_4_0 (
  input  clk,
  input  [1:0] select_A,
  input  [1:0] select_B,
  input  reset,
  input  [1:0] select_C,
  input  WE,
  input  [31:0] C,
  output [31:0] A,
  output [31:0] B
);

  wire decoder_1_out0, decoder_1_out1, decoder_1_out2, decoder_1_out3;
  wire [31:0] register_1_q, register_2_q, register_3_q, register_4_q;

  Decoder #(.select(2), .disabled(0)) decoder_1 (
    .out0(decoder_1_out0), .out1(decoder_1_out1), .out2(decoder_1_out2), .out3(decoder_1_out3),
    .sel(select_C), .en(WE));
  Register #(.width(32)) register_1 (.D({32{1'b0}}), .en(decoder_1_out0), .Q(register_1_q), .clk(clk), .clr(reset));
  Register #(.width(32)) register_2 (.D(C), .en(decoder_1_out1), .Q(register_2_q), .clk(clk), .clr(reset));
  Register #(.width(32)) register_3 (.D(C), .en(decoder_1_out2), .Q(register_3_q), .clk(clk), .clr(reset));
  Register #(.width(32)) register_4 (.D(C), .en(decoder_1_out3), .Q(register_4_q), .clk(clk), .clr(reset));
  Multiplexer #(.select(2), .width(32)) multiplexer_1 (
    .in0(register_1_q), .in1(register_2_q), .in2(register_3_q), .in3(register_4_q), .out(A), .sel(select_A));  // open: en
  Multiplexer #(.select(2), .width(32)) multiplexer_2 (
    .in0(register_1_q), .in1(register_2_q), .in2(register_3_q), .in3(register_4_q), .out(B), .sel(select_B));  // open: en
endmodule

module Adder (
  input  [31:0] A,
  input  [31:0] B,
  output [31:0] C,
  output [1:0] V
);

  wire adder_1_cout;

  Adder_part #(.width(31)) adder_1 (.a(A[30:0]), .b(B[30:0]), .out(C[30:0]), .cout(adder_1_cout));  // open: cin
  Adder_part #(.width(1)) adder_2 (.a(A[31]), .b(B[31]), .out(C[31]), .cin(adder_1_cout), .cout(V[1]));
  xor xor_1 (V[0], adder_1_cout, V[1]);
endmodule

module Subtracter (
  input  [31:0] A,
  input  [31:0] B,
  output [31:0] C,
  output [1:0] V
);

  wire subtractor_1_bout;

  Subtractor #(.width(31)) subtractor_1 (
    .a(A[30:0]), .b(B[30:0]), .out(C[30:0]), .bout(subtractor_1_bout));  // open: bin
  Subtractor #(.width(1)) subtractor_2 (.a(A[31]), .b(B[31]), .out(C[31]), .bin(subtractor_1_bout), .bout(V[1]));
  xor xor_1 (V[0], subtractor_1_bout, V[1]);
endmodule
